# Fritzing sketch plantstalk (saved by Fritzing 0.9.3b)
breadboards: 1

parts:
  Raspberry_Pi_1 = Raspberry Pi 3 [part_number=RPI-3-V1.2]
  Part1 = Adafruit T-Cobbler Plus [part_number="Adafruit #1989 and #2028"]
  DHT1 = DHT22 Humidity and Temperature Sensor
  Part2 = Adafruit BMP180
  DS2 = DS18B20 1-Wire Temperature Sensor [part_number=DS18B20]
  R1 = Resistor [tolerance=±5% resistance=10k package=THT]

nets:
  3V3: Raspberry_Pi_1.3v3, Raspberry_Pi_1.3V3, Part1.+3.3V, Part1.+3.3V_2, DHT1.VDD, Part2.+5V, R1.Pin_1
  N1: Raspberry_Pi_1.GPIO2, Part1.SDA, Part2.SDA
  N2: Raspberry_Pi_1.GPIO3, Part1.SCL, Part2.SCL
  N3: Raspberry_Pi_1.GPIO4, Part1.GPIO4, DS2.DQ
  GND: Raspberry_Pi_1.GND, Part1.GND, DHT1.GND, Part2.GND, DS2.GND
  N4: Raspberry_Pi_1.GPIO17, Part1.GPIO17
  N5: Raspberry_Pi_1.GPIO27, Part1.GPIO27
  N6: Raspberry_Pi_1.GPIO22, Part1.GPIO22
  N7: Raspberry_Pi_1.GPIO10, Part1.MOSI
  N8: Raspberry_Pi_1.GPIO9, Part1.MISO
  N9: Raspberry_Pi_1.GPIO11, Part1.SCLK
  N10: Raspberry_Pi_1.ID_SD, Part1.EEDAT
  N11: Raspberry_Pi_1.GPIO5, Part1.GPIO5, DHT1.DATA, R1.Pin_0
  N12: Raspberry_Pi_1.GPIO6, Part1.GPIO6
  N13: Raspberry_Pi_1.GPIO13, Part1.GPIO13
  N14: Raspberry_Pi_1.GPIO19, Part1.GPIO19
  N15: Raspberry_Pi_1.GPIO26, Part1.GPIO26
  N16: Raspberry_Pi_1.GPIO21, Part1.GPIO21
  N17: Raspberry_Pi_1.GPIO20, Part1.GPIO20
  N18: Raspberry_Pi_1.GPIO16, Part1.GPIO16
  N19: Raspberry_Pi_1.GPIO12, Part1.GPIO12
  N20: Raspberry_Pi_1.ID_SC, Part1.EECLK
  N21: Raspberry_Pi_1.GPIO7, Part1.CE1
  N22: Raspberry_Pi_1.GPIO8, Part1.CE0
  N23: Raspberry_Pi_1.GPIO25, Part1.GPIO25
  N24: Raspberry_Pi_1.GPIO24, Part1.GPIO24
  N25: Raspberry_Pi_1.GPIO23, Part1.GPIO23
  N26: Raspberry_Pi_1.GPIO18, Part1.GPIO18
  N27: Raspberry_Pi_1.GPIO15, Part1.RXD
  N28: Raspberry_Pi_1.GPIO14, Part1.TXD
  5V: Raspberry_Pi_1.5V, Part1.+5V, DS2.VDD

custom parts:
  Adafruit T-Cobbler Plus: The Raspberry Pi has landed on the Maker World like a 40-GPIO pinned, quad-USB ported, credit card sized bomb of DIY joy. And while you can use most of our great Model B accessories by hooking up our downgrade cable, its probably a good time to upgrade your set up and accessorize using all of the 40 pins. That's why we now carry the Assembled Adafruit Pi T-Cobbler Plus - Breakout + Cable for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
  Adafruit BMP180: This precision sensor from Bosch is the best low-cost sensing solution for measuring barometric pressure and temperature. Because pressure changes with altitude you can also use it as an altimeter! The sensor is soldered onto a PCB with a 3.3V regulator, I2C level shifter and pull-up resistors on the I2C pins. The BMP180 is the next-generation of sensors from Bosch, and replaces the BMP085.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
